# Fritzing sketch Task_1 (saved by Fritzing 0.9.3b)
breadboards: 1

parts:
  VCC1 = Battery
  R1 = Rotary Potentiometer (Small) [maximum_resistance=100kΩ package=THT]
  R2 = Resistor [tolerance=±5% resistance=220 package=THT]
  LED1 = LED - 5mm [color="Red (633nm)" package="5 mm [THT]"]

nets:
  N1: VCC1.-, R1.leg1, LED1.cathode
  N2: VCC1.+, R1.leg2
  N3: R1.wiper, R2.Pin_1
  N4: R2.Pin_0, LED1.anode
