# Fritzing sketch Task_2 (saved by Fritzing 0.9.3b)
breadboards: 1

parts:
  VCC1 = Battery
  S1 = Pushbutton [package="[THT]"]
  R1 = Resistor [tolerance=±5% resistance=220 package=THT]
  LED1 = LED - 5mm [color="Red (633nm)" package="5 mm [THT]"]
  R2 = Resistor [tolerance=±5% resistance=220 package=THT]
  R3 = Resistor [tolerance=±5% resistance=220 package=THT]
  R4 = Resistor [tolerance=±5% resistance=220 package=THT]
  LED2 = LED - 5mm [color="Red (633nm)" package="5 mm [THT]"]  # not connected

nets:
  N1: VCC1.-, LED1.cathode, R3.Pin_1, R4.Pin_0
  N2: VCC1.+, S1.Pin_3, S1.Pin_4, R2.Pin_0
  N3: S1.Pin_1, S1.Pin_2, R1.Pin_0
  N4: R1.Pin_1, LED1.anode, R4.Pin_1
  N5: R2.Pin_1, R3.Pin_0
